# Fritzing sketch smart-plant-proto01 (saved by Fritzing 0.9.3b)
breadboards: 1

parts:
  U1 = Mystery Part - 10 pins [part_number=ADS1015 chip_label=? package=THT]
  R1 = Resistor [tolerance=±5% resistance=10k package=THT]
  R2 = Resistor [tolerance=±5% resistance=10k package=THT]
  Photo_IC_diode_S9648-100 = LED - 5mm [color="White (4500K)" package="5 mm [THT]"]
  R3 = Resistor [tolerance=±5% resistance=100 package=THT]
  R4 = Resistor [tolerance=±5% resistance=1k package=THT]
  ESPr1 = ESPr Developper [package="DIP (Dual Inline) [THT]"]

nets:
  3.3V: U1.VDD, R1.Pin_0, R2.Pin_0, R3.Pin_0, ESPr1.3V3
  GND: U1.GND, R4.Pin_1, ESPr1.GND#8
  N1: U1.SCL, R1.Pin_1, ESPr1.IO5
  N2: U1.SDA, R2.Pin_1, ESPr1.IO4
  N3: U1.A0, Photo_IC_diode_S9648-100.cathode, R4.Pin_0
  N4: Photo_IC_diode_S9648-100.anode, R3.Pin_1

custom parts:
  Mystery Part - 10 pins: ADS1015 12-Bit ADC - 4 Channel with Programmable Gain Amplifier https://www.adafruit.com/products/1083
  ESPr Developper: https://www.switch-science.com/catalog/2652/
