# Fritzing sketch smart-plant-proto02 (saved by Fritzing 0.9.3b)
breadboards: 1

parts:
  U1 = Mystery Part - 10 pins [part_number=ADS1015 chip_label=? package=THT]
  R1 = Resistor [tolerance=±5% resistance=10k package=THT]
  R2 = Resistor [tolerance=±5% resistance=10k package=THT]
  R3 = Resistor [tolerance=±5% resistance=47k package=THT]
  ESPr1 = ESPr Developper [package="DIP (Dual Inline) [THT]"]
  Q1 = LTR-301 [package=ltr-301]

nets:
  3.3V: U1.VDD, R1.Pin_0, R2.Pin_0, ESPr1.3V3, Q1.C
  GND: U1.GND, R3.Pin_1, ESPr1.GND#8
  N1: U1.SCL, R1.Pin_1, ESPr1.IO5
  N2: U1.SDA, R2.Pin_1, ESPr1.IO4
  N3: U1.A0, R3.Pin_0, Q1.E

custom parts:
  Mystery Part - 10 pins: ADS1015 12-Bit ADC - 4 Channel with Programmable Gain Amplifier https://www.adafruit.com/products/1083
  ESPr Developper: https://www.switch-science.com/catalog/2652/
