# Fritzing sketch smart-plant-proto03 (saved by Fritzing 0.9.3b)
circuit board: 8.46667cm x 5.64444cm
breadboards: 1

parts:
  U1 = Mystery Part - 10 pins [part_number=ADS1015 chip_label=? package=THT]
  R1 = Resistor [tolerance=±5% resistance=10k package=THT]
  R2 = Resistor [tolerance=±5% resistance=10k package=THT]
  R3 = Resistor [tolerance=±5% resistance=47k package=THT]
  Q1 = LTR-301 [package=ltr-301]
  U2 = mystery part, 4 pins [chip_label=?]
  ESPr1 = ESPr Developper [package="DIP (Dual Inline) [THT]"]

nets:
  3.3V: U1.VDD, R1.Pin_0, R2.Pin_0, Q1.C, U2.pin3, ESPr1.3V3
  GND: U1.GND, R3.Pin_1, U2.pin4, ESPr1.GND#0
  N1: U1.SCL, R1.Pin_1, ESPr1.IO5
  N2: U1.SDA, R2.Pin_1, ESPr1.IO4
  N3: U1.A0, R3.Pin_0, Q1.E
  N4: U1.A3, U2.pin1

custom parts:
  Mystery Part - 10 pins: ADS1015 12-Bit ADC - 4 Channel with Programmable Gain Amplifier https://www.adafruit.com/products/1083
  ESPr Developper: https://www.switch-science.com/catalog/2652/
